# Fritzing sketch pi-2motors-maxbotix (saved by Fritzing 0.7.12b)

parts:
  SONAR1 = Maxbotix MaxSonar Ultrasonic Sensor
  M1 = DC Motor
  M2 = DC Motor
  IC1 = IC, DIP package, 16 pins [chip_label="SN754410 "]
  9V1 = 9V Battery
  RaspberryPi1 = Raspberry Pi Model B
  U1 = Voltage Regulator - 5V [package="TO220 [THT]"]
  CONN1 = USB connector [package=THT]

nets:
  GND: SONAR1.GND, IC1.pin4, IC1.pin5, IC1.pin12, IC1.pin13, 9V1.-, RaspberryPi1.GND, U1.GND, CONN1.d+
  +5V: SONAR1.+5V, IC1.pin16, RaspberryPi1.5V, U1.output_voltage
  N1: SONAR1.PW, RaspberryPi1.#18
  N2: M1.pin_1, IC1.pin14
  N3: M1.pin_2, IC1.pin11
  N4: M2.pin_1, IC1.pin6
  N5: M2.pin_2, IC1.pin3
  N6: IC1.pin1, RaspberryPi1.#17
  N7: IC1.pin2, RaspberryPi1.#21
  N8: IC1.pin7, RaspberryPi1.#22
  N9: IC1.pin8, 9V1.+, U1.input_voltage
  N10: IC1.pin9, RaspberryPi1.#25
  N11: IC1.pin10, RaspberryPi1.#24
  N12: IC1.pin15, RaspberryPi1.#23
  N13: RaspberryPi1.TXD, CONN1.chassis5, CONN1.chassis6
  N14: RaspberryPi1.RXD, CONN1.5V

notes:
  7.4v li-po
  battery
  5v voltage regulator
  or mini DC-DC stepdown converter
  serial
  adapter

custom parts:
  Maxbotix MaxSonar Ultrasonic Sensor: Maxbotix MaxSonar Ultrasonic Sensor LV-EZ0, LV-EZ1, LV-EZ2, LV-EZ3, LV-EZ4
  9V Battery: A nine volt battery
  Raspberry Pi Model B: Raspberry Pi (Model B)
